// Logisim project diagrama5.circ as structural Verilog: 1 circuit, main circuit main
module main (
  input  B2,
  input  B1,
  input  B0
);

  wire and_1_out, and_2_out, and_3_out, and_4_out, and_5_out, not_1_out, not_2_out, not_3_out, or_1_out;

  not not_1 (not_1_out, B2);
  not not_2 (not_2_out, B1);
  not not_3 (not_3_out, B0);
  and and_1 (and_1_out, not_1_out, not_2_out, not_3_out);
  and and_2 (and_2_out, B1, B0);
  and and_3 (and_3_out, B2, B0);
  and and_4 (and_4_out, B2, not_2_out);
  and and_5 (and_5_out, B2, B1);
  or or_1 (or_1_out, and_1_out, and_2_out, and_3_out);
  LED Y1 (.in(or_1_out));
  LED Y2 (.in(and_4_out));
  LED Y3 (.in(and_5_out));
  LED Y0 (.in(1'b1));
endmodule
